// Logisim project cpu.circ as structural Verilog: 5 circuits, main circuit main
module main (
);

  wire Clk_out, Reset_out, undriven_4;
  wire [7:0] memory_1_do, pc_1_adho, pc_1_adlo, undriven_2, undriven_3, undriven_5;
  wire [13:1] undriven;

  Button Reset (.out(Reset_out));
  Button Clk (.out(Clk_out));
  PC pc_1 (
    .Reset(Reset_out), .CE(undriven[1]), .Clk(Clk_out), .ADLI(pc_1_adlo), .ADHI(pc_1_adho), .OE(undriven[2]),
    .ADLO(pc_1_adlo), .ADHO(pc_1_adho));
  Memory memory_1 (
    .WE(undriven[4]), .Clk(Clk_out), .DI(memory_1_do), .ADL(pc_1_adho), .ADH(pc_1_adlo), .OE(undriven[3]),
    .DO(memory_1_do));
  // Probe on {undriven_3, undriven_2}
  Registers registers_1 (
    .AWE(undriven[8]), .XWE(undriven_4), .YWE(undriven[12]), .DBI(memory_1_do), .Clk(Clk_out),
    .Reset(Reset_out), .AO(undriven_5), .AOE(undriven[9]), .XOE(undriven[11]), .YOE(undriven[13]),
    .DBO(memory_1_do));
  ALU alu_1 (
    .AI(undriven_5), .DBI(memory_1_do), .DBO(memory_1_do));  // open: BOr, BXOr, Shl, Shr, BNot, Inc, Dec, OE, Add, Sub, Mul, Div, BAnd, C
endmodule

module Memory (
  input  WE,
  input  Clk,
  input  [7:0] DI,
  input  OE,
  input  [7:0] ADL,
  input  [7:0] ADH,
  output [7:0] DO
);

  wire and_1_out, not_1_out, not_2_out;
  wire [7:0] controlled_buffer_1_out, ram_1_dout, rom_1_data;

  not not_1 (not_1_out, ADH[7]);
  RAM #(.addrWidth(15)) ram_1 (
    .addr({ADH[6:0], ADL}), .we(and_1_out), .oe(1'b1), .clk(Clk), .din(DI), .dout(ram_1_dout));
  and and_1 (and_1_out, WE, not_1_out);
  ROM #(.addrWidth(15)) rom_1 (.addr({ADH[6:0], ADL}), .data(rom_1_data));
  assign controlled_buffer_1_out = not_2_out ? ram_1_dout : 8'bz;  // Controlled_Buffer controlled_buffer_1
  not not_2 (not_2_out, ADH[7]);
  assign DO = OE ? controlled_buffer_1_out : 8'bz;  // Controlled_Buffer controlled_buffer_2
  assign controlled_buffer_1_out = ADH[7] ? rom_1_data : 8'bz;  // Controlled_Buffer controlled_buffer_3
endmodule

module PC (
  input  Reset,
  input  CE,
  input  Clk,
  input  OE,
  input  [7:0] ADLI,
  input  [7:0] ADHI,
  output [7:0] ADLO,
  output [7:0] ADHO
);

  wire [15:0] counter_1_q;

  Counter #(.max('hffff), .width(16)) counter_1 (
    .clr(Reset), .up(1'b1), .count(CE), .clk(Clk), .D({ADHI, ADLI}), .Q(counter_1_q));  // open: load, carry
  assign {ADHO, ADLO} = OE ? counter_1_q : 16'bz;  // Controlled_Buffer controlled_buffer_1
endmodule

module Registers (
  input  Clk,
  input  Reset,
  input  [7:0] DBI,
  input  [7:0] AO,
  input  AOE,
  input  AWE,
  input  XOE,
  input  XWE,
  input  YOE,
  input  YWE,
  output [7:0] DBO
);

  wire [7:0] register_2_q, register_3_q;

  Register register_1 (.D(DBI), .en(AWE), .clk(Clk), .Q(AO), .clr(Reset));
  Register register_2 (.D(DBI), .en(XWE), .clk(Clk), .Q(register_2_q), .clr(Reset));
  Register register_3 (.D(DBI), .en(YWE), .clk(Clk), .Q(register_3_q), .clr(Reset));
  assign DBO = AOE ? AO : 8'bz;  // Controlled_Buffer controlled_buffer_1
  assign DBO = XOE ? register_2_q : 8'bz;  // Controlled_Buffer controlled_buffer_2
  assign DBO = YOE ? register_3_q : 8'bz;  // Controlled_Buffer controlled_buffer_3
endmodule

module ALU (
  input  Add,
  input  Sub,
  input  Mul,
  input  Div,
  input  BAnd,
  input  BOr,
  input  BXOr,
  input  Shl,
  input  Shr,
  input  BNot,
  input  Inc,
  input  Dec,
  input  [7:0] AI,
  input  [7:0] DBI,
  input  OE,
  output [7:0] DBO,
  output C
);

  wire adder_1_cout, subtractor_1_bout;
  wire [7:0] adder_1_out, adder_2_out, and_2_out, controlled_buffer_1_out, divider_1_out, multiplier_1_cout,
       multiplier_1_out, not_1_out, or_1_out, shifter_1_out, shifter_2_out, subtractor_1_out,
       subtractor_2_out, xor_1_out;

  assign controlled_buffer_1_out = Add ? adder_1_out : 8'bz;  // Controlled_Buffer controlled_buffer_1
  Adder adder_1 (.a(AI), .b(DBI), .out(adder_1_out), .cout(adder_1_cout));  // open: cin
  assign C = Add ? adder_1_cout : 1'bz;  // Controlled_Buffer controlled_buffer_2
  assign controlled_buffer_1_out = Sub ? subtractor_1_out : 8'bz;  // Controlled_Buffer controlled_buffer_3
  Subtractor subtractor_1 (.a(AI), .b(DBI), .out(subtractor_1_out), .bout(subtractor_1_bout));  // open: bin
  assign C = Sub ? subtractor_1_bout : 1'bz;  // Controlled_Buffer controlled_buffer_4
  assign controlled_buffer_1_out = Mul ? multiplier_1_out : 8'bz;  // Controlled_Buffer controlled_buffer_5
  Multiplier multiplier_1 (.b(DBI), .out(multiplier_1_out), .cout(multiplier_1_cout));  // open: a, cin
  assign controlled_buffer_1_out = Div ? divider_1_out : 8'bz;  // Controlled_Buffer controlled_buffer_6
  Divider divider_1 (.a(AI), .b(DBI), .out(divider_1_out));  // open: upper, rem
  and and_1 (C, multiplier_1_cout[0], multiplier_1_cout[1], multiplier_1_cout[2], multiplier_1_cout[3], multiplier_1_cout[4], multiplier_1_cout[5], multiplier_1_cout[6], multiplier_1_cout[7]);
  assign and_2_out = AI & DBI;  // AND_Gate and_2, 8 bits wide
  assign controlled_buffer_1_out = BAnd ? and_2_out : 8'bz;  // Controlled_Buffer controlled_buffer_7
  assign or_1_out = AI | DBI;  // OR_Gate or_1, 8 bits wide
  assign controlled_buffer_1_out = BOr ? or_1_out : 8'bz;  // Controlled_Buffer controlled_buffer_8
  assign xor_1_out = AI ^ DBI;  // XOR_Gate xor_1, 8 bits wide
  assign controlled_buffer_1_out = BXOr ? xor_1_out : 8'bz;  // Controlled_Buffer controlled_buffer_9
  Shifter shifter_1 (.in(AI), .\dist (DBI[2:0]), .out(shifter_1_out));
  Shifter #(.shift("lr")) shifter_2 (.in(AI), .\dist (DBI[2:0]), .out(shifter_2_out));
  assign not_1_out = ~AI;  // NOT_Gate not_1, 8 bits wide
  Adder adder_2 (.a(AI), .b({8{1'b0}}), .out(adder_2_out), .cin(1'b1));  // open: cout
  Subtractor subtractor_2 (.a(AI), .b({8{1'b0}}), .out(subtractor_2_out), .bin(1'b1));  // open: bout
  assign controlled_buffer_1_out = Shl ? shifter_1_out : 8'bz;  // Controlled_Buffer controlled_buffer_10
  assign controlled_buffer_1_out = Shr ? shifter_2_out : 8'bz;  // Controlled_Buffer controlled_buffer_11
  assign controlled_buffer_1_out = BNot ? not_1_out : 8'bz;  // Controlled_Buffer controlled_buffer_12
  assign controlled_buffer_1_out = Inc ? adder_2_out : 8'bz;  // Controlled_Buffer controlled_buffer_13
  assign controlled_buffer_1_out = Dec ? subtractor_2_out : 8'bz;  // Controlled_Buffer controlled_buffer_14
  assign DBO = OE ? controlled_buffer_1_out : 8'bz;  // Controlled_Buffer controlled_buffer_15
endmodule
